# Fritzing sketch flight-computer (saved by Fritzing 0.9.3b)

parts:
  FeatherWing_M0_Adalogger = Adafruit Feather M0 Adalogger [part_number="Adafruit #2796"]
  Gyro_Accelerometer_Compass = Adafruit FXOS8700 + FXAS21002 9 DoF Breakout [part_number="Adafruit #3463"]
  Barometric_Pressure_Sensor_(Altimeter) = Adafruit_BMP280
  Featherwing_GPS = Adafruit Ultimate GPS v3 [part_number="Adafruit #746"]
  Elevator_Control = Basic Servo
  Aileron_Control = Basic Servo
  ESC_with_Battery_Elimination_Circuit = ESC 30A
  DC_Motor = DJI 920 KV Motor
  LIPO_11_7v_1800mAh = LIPO-2000mAh [package=lipo-2000]

nets:
  GND: FeatherWing_M0_Adalogger.GND, Gyro_Accelerometer_Compass.GND, Barometric_Pressure_Sensor_(Altimeter).GND, Featherwing_GPS.GND, Elevator_Control.gnd, Aileron_Control.gnd, ESC_with_Battery_Elimination_Circuit.GND#4
  N1: FeatherWing_M0_Adalogger.D1, Featherwing_GPS.TX
  N2: FeatherWing_M0_Adalogger.D0, Featherwing_GPS.RX
  VIN: FeatherWing_M0_Adalogger.+3V3, Gyro_Accelerometer_Compass.VIN, Featherwing_GPS.VIN
  VCC: FeatherWing_M0_Adalogger.VBAT, Elevator_Control.vcc, Aileron_Control.vcc, ESC_with_Battery_Elimination_Circuit.v+
  N3: FeatherWing_M0_Adalogger.D13, ESC_with_Battery_Elimination_Circuit.In
  N4: FeatherWing_M0_Adalogger.D12, Barometric_Pressure_Sensor_(Altimeter).SDO/ADR
  N5: FeatherWing_M0_Adalogger.D11, Barometric_Pressure_Sensor_(Altimeter).SDI/SDA
  N6: FeatherWing_M0_Adalogger.D10, Barometric_Pressure_Sensor_(Altimeter).SCK/SCL
  N7: FeatherWing_M0_Adalogger.D9, Barometric_Pressure_Sensor_(Altimeter).CS
  N8: FeatherWing_M0_Adalogger.D6, Elevator_Control.pulse
  N9: FeatherWing_M0_Adalogger.D5, Aileron_Control.pulse
  N10: FeatherWing_M0_Adalogger.SCL, Gyro_Accelerometer_Compass.SCL
  N11: FeatherWing_M0_Adalogger.SDA, Gyro_Accelerometer_Compass.SDA
  N12: ESC_with_Battery_Elimination_Circuit.GND#5, LIPO_11_7v_1800mAh.-
  N13: ESC_with_Battery_Elimination_Circuit.A, DC_Motor.u
  N14: ESC_with_Battery_Elimination_Circuit.B, DC_Motor.v
  N15: ESC_with_Battery_Elimination_Circuit.C, DC_Motor.w
  N16: ESC_with_Battery_Elimination_Circuit.V+, LIPO_11_7v_1800mAh.+

custom parts:
  Adafruit Feather M0 Adalogger: This is the Adafruit Feather M0 Adalogger - our take on an 'all-in-one' Cortex M0 datalogger (or data-reader) with built in USB and battery charging. Its an Adafruit Feather M0 with a microSD holder ready to rock! We have other boards in the Feather family, check'em out here At the Feather M0's heart is an ATSAMD21G18 ARM Cortex M0 processor, clocked at 48 MHz and at 3.3V logic, the same one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
  Adafruit FXOS8700 + FXAS21002 9 DoF Breakout: The NXP Precision 9DoF breakout combines two of the best motion sensors we've tested here at Adafruit: The FXOS8700 3-Axis accelerometer and magnetometer, and the FXAS21002 3-axis gyroscope. These two sensors combine to make a nice 9-DoF kit, that can be used for motion and orientation sensing. In particular, we think this sensor set is ideal for AHRS-based orientation calculations: the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
  Adafruit_BMP280: Bosch has stepped up their game with their new BMP280 sensor, an environmental sensor with temperature, barometric pressure that is the next generation upgrade to the BMP085/BMP180/BMP183. This sensor is great for all sorts of weather sensing and can even be used in both I2C and SPI! This precision sensor from Bosch is the best low-cost, precision sensing solution for measuring barometric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
  Adafruit Ultimate GPS v3: We carry a few different GPS modules here in the Adafruit shop, but none that satisfied our every desire - that's why we designed this little GPS breakout board. We believe this is the Ultimate GPS module, so we named it that. It's got everything you want and more: -165 dBm sensitivity, 10 Hz updates, 66 channels 5V friendly design and only 20mA current draw Breadboard friendly + two mounting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
  ESC 30A: Electronic Speed Controller - 30A
  DJI 920 KV Motor: DJI Brushless Outrunner 2212/920K Motor F330-550
